# Fritzing sketch IronGeek (saved by Fritzing 0.9.3b)

parts:
  R1 = BBC MicroBit
  Part1 = 24 NeoPixel Ring [part_number=1586]

nets:
  GND: R1.GND, Part1.GND
  3V3: R1.3v3, Part1.VDD
  N1: R1.P0_ANALOG_IN, Part1.IN

custom parts:
  BBC MicroBit: The BBC MICRO:BIT
  24 NeoPixel Ring: 24 ultra bright smart LED NeoPixels are arranged in a circle with 2.6" (66mm) outer diameter. The rings are 'chainable' - connect the output pin of one to the input pin of another. Use only one microcontroller pin to control as many as you can chain together! Each LED is addressable as the driver chip is inside the LED. Each one has ~18mA constant current drive so the color will be very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
