# Fritzing sketch Test-Project (saved by Fritzing 0.9.3b)

parts:
  R1 = BBC MicroBit
  LED1 = LED - 5mm [color="Red (633nm)" package="5 mm [THT]"]

nets:
  N1: R1.GND, LED1.cathode
  N2: R1.P0_ANALOG_IN, LED1.anode

custom parts:
  BBC MicroBit: The BBC MICRO:BIT
